# Fritzing sketch hazzah_to_hx711 (saved by Fritzing 0.9.3b)
breadboards: 1

parts:
  Part1 = Adafruit Feather HUZZAH ESP8266 [part_number="Adafruit #2821"]
  SparkFun_Load_Cell_Amplifier_-_HX1 = SparkFun Load Cell Amplifier - HX711 [part_number=SEN-13879]

nets:
  GND: Part1.GND, SparkFun_Load_Cell_Amplifier_-_HX1.GND
  3.3V: Part1.3.3V, SparkFun_Load_Cell_Amplifier_-_HX1.VDD
  N1: Part1.VBUS, SparkFun_Load_Cell_Amplifier_-_HX1.VCC
  N2: Part1.GPIO5/SCL, SparkFun_Load_Cell_Amplifier_-_HX1.SCK
  N3: Part1.GPIO4/SDA, SparkFun_Load_Cell_Amplifier_-_HX1.DAT

custom parts:
  Adafruit Feather HUZZAH ESP8266: his is the Adafruit Feather HUZZAH ESP8266 - our take on an 'all-in-one' ESP8266 WiFi development board with built in USB and battery charging. Its an ESP8266 WiFi module with all the extras you need, ready to rock! We have other boards in the Feather family, check'em out here. At the Feather HUZZAH's heart is an ESP8266 WiFi microcontroller clocked at 80 MHz and at 3.3V logic. This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
  SparkFun Load Cell Amplifier - HX711: The SparkFun Load Cell Amplifier is a small breakout board for the HX711 IC that allows you to easily read load cells to measure weight. By connecting the amplifier to your microcontroller you will be able to read the changes in the resistance of the load cell, and with some calibration you’ll be able to get very accurate weight measurements. This can be handy for creating your own industrial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
